// Logisim project stargate323_LogisimEvolution.circ as structural Verilog: 1 circuit, main circuit main
module main (
);

  wire clk_out, d_ff_1_q, d_ff_2_qn, d_ff_3_q, d_ff_4_q, d_ff_5_q, d_ff_6_q, d_ff_7_q, d_ff_8_q, d_ff_9_q,
       d_ff_10_q, d_ff_11_q, d_ff_12_q, d_ff_13_q, d_ff_14_q, d_ff_15_q, d_ff_16_q, d_ff_17_q, not_1_out,
       not_2_out, not_3_out, not_4_out, not_5_out;
  wire [7:0] counter_1_q, P0808_data, P0810_data, P0811_data, register_1_q, TIMING_q;
  wire [12:6] PDL_p1;

  Clock sysclk ();  // open: out
  Clock #(.highDuration(4), .lowDuration(4)) clk (.out(clk_out));
  Counter TIMING (.up(1'b1), .count(1'b1), .clk(clk_out), .Q(TIMING_q));  // open: clr, load, D, carry
  // Probe on TIMING_q
  ROM P0810 (.addr(TIMING_q), .data(P0810_data));
  ROM P0811 (.addr(TIMING_q), .data(P0811_data));
  not not_1 (not_1_out, TIMING_q[1]);
  D_Flip_Flop d_ff_1 (.D(not_1_out), .clk(clk_out), .Q(d_ff_1_q));  // open: Qn, preset, reset
  D_Flip_Flop d_ff_2 (.D(P0810_data[0]), .clk(clk_out), .Qn(d_ff_2_qn));  // open: Q, preset, reset
  D_Flip_Flop d_ff_3 (.D(P0810_data[1]), .clk(clk_out), .Q(d_ff_3_q));  // open: Qn, preset, reset
  D_Flip_Flop d_ff_4 (.D(P0810_data[2]), .clk(clk_out), .Q(d_ff_4_q));  // open: Qn, preset, reset
  D_Flip_Flop d_ff_5 (.D(P0810_data[3]), .clk(clk_out), .Q(d_ff_5_q));  // open: Qn, preset, reset
  D_Flip_Flop d_ff_6 (.D(P0810_data[4]), .clk(clk_out), .Q(d_ff_6_q));  // open: Qn, preset, reset
  D_Flip_Flop d_ff_7 (.D(P0810_data[5]), .clk(clk_out), .Q(d_ff_7_q));  // open: Qn, preset, reset
  D_Flip_Flop d_ff_8 (.D(P0810_data[6]), .clk(clk_out), .Q(d_ff_8_q));  // open: Qn, preset, reset
  D_Flip_Flop d_ff_9 (.D(P0810_data[7]), .clk(clk_out), .Q(d_ff_9_q));  // open: Qn, preset, reset
  D_Flip_Flop d_ff_10 (.D(P0811_data[0]), .clk(clk_out), .Q(d_ff_10_q));  // open: Qn, preset, reset
  D_Flip_Flop d_ff_11 (.D(P0811_data[1]), .clk(clk_out), .Q(d_ff_11_q));  // open: Qn, preset, reset
  D_Flip_Flop d_ff_12 (.D(P0811_data[2]), .clk(clk_out), .Q(d_ff_12_q));  // open: Qn, preset, reset
  D_Flip_Flop d_ff_13 (.D(P0811_data[3]), .clk(clk_out), .Q(d_ff_13_q));  // open: Qn, preset, reset
  D_Flip_Flop d_ff_14 (.D(P0811_data[4]), .clk(clk_out), .Q(d_ff_14_q));  // open: Qn, preset, reset
  D_Flip_Flop d_ff_15 (.D(P0811_data[5]), .clk(clk_out), .Q(d_ff_15_q));  // open: Qn, preset, reset
  D_Flip_Flop d_ff_16 (.D(P0811_data[6]), .clk(clk_out), .Q(d_ff_16_q));  // open: Qn, preset, reset
  D_Flip_Flop d_ff_17 (.D(P0811_data[7]), .clk(clk_out), .Q(d_ff_17_q));  // open: Qn, preset, reset
  not not_2 (not_2_out, d_ff_1_q);
  // Probe on d_ff_2_qn
  Counter counter_1 (
    .clr(d_ff_2_qn), .up(1'b1), .count(1'b1), .clk(not_3_out), .Q(counter_1_q));  // open: load, D, carry
  not not_3 (not_3_out, not_2_out);
  // Probe on d_ff_3_q
  not not_4 (not_4_out, d_ff_3_q);
  // Probe on d_ff_4_q
  // Probe on d_ff_5_q
  // Probe on d_ff_6_q
  // Probe on d_ff_7_q
  // Probe on d_ff_8_q
  // Probe on d_ff_9_q
  // Probe on d_ff_10_q
  // Probe on d_ff_11_q
  // Probe on d_ff_12_q
  // Probe on d_ff_13_q
  // Probe on d_ff_14_q
  // Probe on d_ff_15_q
  // Probe on d_ff_16_q
  // Probe on d_ff_17_q
  // Probe on not_4_out
  // Probe on d_ff_1_q
  // Probe on counter_1_q[0]
  // Probe on counter_1_q[1]
  // Probe on counter_1_q[2]
  // Probe on counter_1_q[3]
  // Probe on counter_1_q[4]
  // Probe on counter_1_q[5]
  // DipSwitch #(.number(4)) PDL: pin names not known; wires that end beside it: PDL_p1[6], PDL_p1[7], PDL_p1[8], PDL_p1[12]
  // DipSwitch #(.number(3)) PGM: pin names not known; wires that end beside it: PDL_p1[9], PDL_p1[10], PDL_p1[11]
  ROM #(.addrWidth(13)) P0808 (.addr({PDL_p1, counter_1_q[5:0]}), .data(P0808_data));
  not not_5 (not_5_out, d_ff_9_q);
  // Probe on not_5_out
  Register register_1 (.D(P0808_data), .en(1'b1), .clk(d_ff_1_q), .Q(register_1_q));  // open: clr
  // Probe on P0808_data
  // Probe on register_1_q

  // Notes on the sheet:
  //   contents of P0810 (hex, n*v repeats v):
  //   e4 e4 e4 e5 e5 c5 5*e5 c5 4*e5 c5 e5 e5 e5 c5 e5 e5 e5 c5 e5 e5 c5 e5 e5 c5 e5 85 a5 e5 e5 e5 c5 e5
  //   e5 e5 c5 e5 e5 e5 c5 e5 e5 e5 c5 e5 e5 c5 e5 e5 c5 e5 e5 d5 f5 75 55 75 7d fb 9b a3 f3 73 73 7b 7b
  //   ff fb e3 f3 73 73 7b 7b ff fb e3 f3 73 73 7b 7b ff fb e3 f3 73 73 7b 7b ff fb e3 f3 73 73 7b 7b ff
  //   fb e3 f3 73 73 7b 7b ff fb e3 f3 73 73 7b 7b ff fb e3 f3 73 73 7b 7b ff fb e3 f3 73 73 7b 7b ff fb
  //   e3 f3 73 73 7b 7b ff fb e3 f3 73 73 7b 7b ff fb e3 f3 73 73 7b 7b ff fb e3 f3 73 73 7b 7b ff fb e3
  //   f3 73 73 7b 7b ff fb e3 f3 f3 f3 fb fb ff fb e3 f3 f3 f3 fb fb ff fb e3 f3 f3 f3 fb fb ff fb e3 f3
  //   f3 f3 fb fb ff fb e3 f3 f3 f3 fb fb ff fb e3 f3 f3 f3 fb fb ff fb e3 f3 f3 f3 fb fb ff fb e3 f3 f3
  //   f3 fb fb ff fb e3 f3 f3 f3 fb fb ff fb e3 e3 eb e2 c2 e2
  //   contents of P0811 (hex, n*v repeats v):
  //   32*7d 24*bd 8*bc 4*3e 4*1e 4*3e 4*2e 4*3e 4*2e 4*3e 4*2e 4*3e 4*2e 4*3e 4*2e 4*3e 4*2e 4*3e 4*2e
  //   4*3e 4*2e 4*3e 4*2e 4*3e 4*2e 4*3e 4*2e 4*3e 4*2e 4*3e 4*2e 4*3e 4*2e 4*3e 4*2e 4*3e 4*36 4*3e 4*36
  //   3e 3c 3c 3c 4*34 4*3c 4*34 4*3c 4*38 4*3c 4*38 4*3c 4*38 4*3d 4*39
  //   contents of P0808 (hex, n*v repeats v):
  //   16*0 5 0 7 0 9 0 b 0 e 0 10 0 14 0 16 0 17 0 19 0 1c 0 1f 0 21 0 23 0 25 90 6 40 5 f0 3 a0 2 c0 9 80
  //   7 40 5 0 3 19*0 5 0 7 0 9 0 b 0 e 0 10 0 14 0 16 0 17 0 19 0 1c 0 1f 0 21 0 23 0 25 d0 7 80 6 30 5
  //   e0 3 0 b c0 8 80 6 40 4 19*0 5 0 7 0 9 0 b 0 e 0 10 0 14 0 16 0 17 0 19 0 1c 0 1f 0 21 0 23 0 25 50
  //   5 0 4 b0 2 60 1 80 8 40 6 0 4 c0 1 19*0 5 0 7 0 9 0 b 0 e 0 10 0 14 0 16 0 17 0 19 0 1c 0 1f 0 21 0
  //   23 0 25 10 4 c0 2 70 1 20 0 40 7 0 5 c0 2 80 20*0 5 0 7 0 9 0 b 0 e 0 10 0 14 0 16 0 17 0 19 0 1c 0
  //   1f 0 21 0 23 0 25 50 a 0 9 b0 7 60 6 80 d 40 b 0 9 c0 6 19*0 5 0 7 0 9 0 b 0 e 0 10 0 14 0 16 0 17 0
  //   19 0 1c 0 1f 0 21 0 23 0 25 10 9 c0 7 70 6 20 5 40 c 0 a c0 7 80 5 19*0 5 0 7 0 9 0 b 0 e 0 10 0 14
  //   0 16 0 17 0 19 0 1c 0 1f 0 21 0 23 0 25 90 b 40 a f0 8 a0 7 c0 e 80 c 40 a 0 8 19*0 5 0 7 0 9 0 b 0
  //   e 0 10 0 14 0 16 0 17 0 19 0 1c 0 1f 0 21 0 23 0 25 10 e c0 c 70 b 20 a 40 11 0 f c0 c 80 a 19*0 8 0
  //   a 0 b 0 10 0 11 0 15 0 16 0 19 0 1c 0 1f 0 22 0 24 0 27 0 2a 0 2c e0 7 20 6 60 4 a0 2 20 c 20 9 20 6
  //   20 3 19*0 8 0 a 0 b 0 10 0 11 0 15 0 16 0 19 0 1c 0 1f 0 22 0 24 0 27 0 2a 0 2c 20 9 60 7 a0 5 e0 3
  //   60 d 60 a 60 7 60 4 19*0 8 0 a 0 b 0 10 0 11 0 15 0 16 0 19 0 1c 0 1f 0 22 0 24 0 27 0 2a 0 2c a0 6
  //   e0 4 20 3 60 1 e0 a e0 7 e0 4 e0 1 19*0 8 0 a 0 b 0 10 0 11 0 15 0 16 0 19 0 1c 0 1f 0 22 0 24 0 27
  //   0 2a 0 2c 60 5 a0 3 e0 1 20 0 a0 9 a0 6 a0 3 a0 20*0 8 0 a 0 b 0 10 0 11 0 15 0 16 0 19 0 1c 0 1f 0
  //   22 0 24 0 27 0 2a 0 2c a0 b e0 9 20 8 60 6 e0 f e0 c e0 9 e0 6 19*0 8 0 a 0 b 0 10 0 11 0 15 0 16 0
  //   19 0 1c 0 1f 0 22 0 24 0 27 0 2a 0 2c 60 a a0 8 e0 6 20 5 a0 e a0 b a0 8 a0 5 19*0 8 0 a 0 b 0 10 0
  //   11 0 15 0 16 0 19 0 1c 0 1f 0 22 0 24 0 27 0 2a 0 2c e0 c 20 b 60 9 a0 7 20 11 20 e 20 b 20 8 19*0 8
  //   0 a 0 b 0 10 0 11 0 15 0 16 0 19 0 1c 0 1f 0 22 0 24 0 27 0 2a 0 2c 60 f a0 d e0 b 20 a a0 13 a0 10
  //   a0 d a0 a 19*0 3 0 5 0 6 0 8 0 b 0 c 0 e 0 11 0 12 0 14 0 17 0 18 0 19 0 1d 0 1e 40 5 60 4 80 3 a0 2
  //   60 7 e0 5 60 4 e0 2 19*0 3 0 5 0 6 0 8 0 b 0 c 0 e 0 11 0 12 0 14 0 17 0 18 0 19 0 1d 0 1e 80 6 a0 5
  //   c0 4 e0 3 a0 8 20 7 a0 5 20 4 19*0 3 0 5 0 6 0 8 0 b 0 c 0 e 0 11 0 12 0 14 0 17 0 18 0 19 0 1d 0 1e
  //   0 4 20 3 40 2 60 1 20 6 a0 4 20 3 a0 1 19*0 3 0 5 0 6 0 8 0 b 0 c 0 e 0 11 0 12 0 14 0 17 0 18 0 19
  //   0 1d 0 1e c0 2 e0 1 0 1 20 0 e0 4 60 3 e0 1 60 20*0 3 0 5 0 6 0 8 0 b 0 c 0 e 0 11 0 12 0 14 0 17 0
  //   18 0 19 0 1d 0 1e 0 9 20 8 40 7 60 6 20 b a0 9 20 8 a0 6 19*0 3 0 5 0 6 0 8 0 b 0 c 0 e 0 11 0 12 0
  //   14 0 17 0 18 0 19 0 1d 0 1e c0 7 e0 6 0 6 20 5 e0 9 60 8 e0 6 60 5 19*0 3 0 5 0 6 0 8 0 b 0 c 0 e 0
  //   11 0 12 0 14 0 17 0 18 0 19 0 1d 0 1e 40 a 60 9 80 8 a0 7 60 c e0 a 60 9 e0 7 19*0 3 0 5 0 6 0 8 0 b
  //   0 c 0 e 0 11 0 12 0 14 0 17 0 18 0 19 0 1d 0 1e c0 c e0 b 0 b 20 a e0 e 60 d e0 b 60 a 19*0 2 0 4 0
  //   5 0 7 0 8 0 9 0 b 0 d 0 e 0 f 0 10 0 12 0 14 0 15 0 16 f0 3 80 3 10 3 a0 2 0 5 40 4 80 3 c0 2 19*0 2
  //   0 4 0 5 0 7 0 8 0 9 0 b 0 d 0 e 0 f 0 10 0 12 0 14 0 15 0 16 30 5 c0 4 50 4 e0 3 40 6 80 5 c0 4 0 4
  //   19*0 2 0 4 0 5 0 7 0 8 0 9 0 b 0 d 0 e 0 f 0 10 0 12 0 14 0 15 0 16 b0 2 40 2 d0 1 60 1 c0 3 0 3 40
  //   2 80 1 19*0 2 0 4 0 5 0 7 0 8 0 9 0 b 0 d 0 e 0 f 0 10 0 12 0 14 0 15 0 16 70 1 0 1 90 0 20 0 80 2
  //   c0 1 0 1 40 20*0 2 0 4 0 5 0 7 0 8 0 9 0 b 0 d 0 e 0 f 0 10 0 12 0 14 0 15 0 16 b0 7 40 7 d0 6 60 6
  //   c0 8 0 8 40 7 80 6 19*0 2 0 4 0 5 0 7 0 8 0 9 0 b 0 d 0 e 0 f 0 10 0 12 0 14 0 15 0 16 70 6 0 6 90 5
  //   20 5 80 7 c0 6 0 6 40 5 19*0 2 0 4 0 5 0 7 0 8 0 9 0 b 0 d 0 e 0 f 0 10 0 12 0 14 0 15 0 16 f0 8 80
  //   8 10 8 a0 7 0 a 40 9 80 8 c0 7 19*0 2 0 4 0 5 0 7 0 8 0 9 0 b 0 d 0 e 0 f 0 10 0 12 0 14 0 15 0 16
  //   70 b 0 b 90 a 20 a 80 c c0 b 0 b 40 a 19*0 f 0 10 0 11 0 14 0 15 0 19 0 1c 0 20 0 24 0 28 0 2c 0 2f
  //   0 34 0 3b 0 3f 80 a e0 7 40 5 a0 2 e0 10 60 c e0 7 60 3 19*0 f 0 10 0 11 0 14 0 15 0 19 0 1c 0 20 0
  //   24 0 28 0 2c 0 2f 0 34 0 3b 0 3f c0 b 20 9 80 6 e0 3 20 12 a0 d 20 9 a0 4 19*0 f 0 10 0 11 0 14 0 15
  //   0 19 0 1c 0 20 0 24 0 28 0 2c 0 2f 0 34 0 3b 0 3f 40 9 a0 6 0 4 60 1 a0 f 20 b a0 6 20 2 19*0 f 0 10
  //   0 11 0 14 0 15 0 19 0 1c 0 20 0 24 0 28 0 2c 0 2f 0 34 0 3b 0 3f 0 8 60 5 c0 2 20 0 60 e e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
endmodule
